// Digital circuit Suma_resta.dig as structural Verilog
module Suma_resta (
  input  a1,
  input  b1,
  input  a0,
  input  b0,
  input  a3,
  input  b3,
  input  a2,
  input  b2,
  input  Op,
  output s1,
  output s0,
  output s3,
  output s2,
  output s4
);

  wire sumres_1_p4, sumres_2_p4, sumres_3_p4;

  // sumres sumres_1: pin names not known; wires that end beside it: Op, a3, b3, sumres_1_p4, s3, s4
  // sumres sumres_2: pin names not known; wires that end beside it: Op, a2, b2, sumres_2_p4, s2, sumres_1_p4
  // sumres sumres_3: pin names not known; wires that end beside it: Op, a1, b1, sumres_3_p4, s1, sumres_2_p4
  // sumres sumres_4: pin names not known; wires that end beside it: Op, a0, b0, 1'b0, s0, sumres_3_p4

  // Notes on the sheet:
  //   testbech
endmodule
