// Digital circuit base_conversor.dig as structural Verilog
module base_conversor (
  input  e4,
  input  e3,
  input  e2,
  input  e1,
  input  e0,
  output d3,
  output d2,
  output d1,
  output d0,
  output u3,
  output u2,
  output u1,
  output u0
);

  wire and_1_out, and_2_out, and_3_out, and_4_out, and_5_out, and_6_out, and_7_out, and_8_out, and_9_out,
       and_10_out, and_11_out, and_12_out, and_13_out, and_14_out, and_15_out, and_16_out, and_17_out,
       and_18_out, not_1_out, not_2_out, not_3_out, not_4_out;

  not not_1 (not_1_out, e4);
  not not_2 (not_2_out, e3);
  not not_3 (not_3_out, e2);
  not not_4 (not_4_out, e1);
  and and_1 (and_1_out, e2, e4);
  and and_2 (and_2_out, e3, e4);
  and and_3 (and_3_out, e1, e3, not_1_out);
  and and_4 (and_4_out, e1, e2, e3);
  and and_5 (and_5_out, e2, e3, not_1_out);
  and and_6 (and_6_out, not_3_out, not_2_out, e4);
  and and_7 (and_7_out, not_4_out, not_3_out, e3, not_1_out);
  and and_8 (and_8_out, e1, not_3_out, not_2_out, e4);
  and and_9 (and_9_out, not_4_out, e2, e3, e4);
  and and_10 (and_10_out, e1, e2, not_1_out);
  and and_11 (and_11_out, not_4_out, not_3_out, e4);
  and and_12 (and_12_out, e2, not_2_out, not_1_out);
  and and_13 (and_13_out, not_3_out, e3, e4);
  and and_14 (and_14_out, e1, not_2_out, not_1_out);
  and and_15 (and_15_out, not_4_out, e2, e3, not_1_out);
  and and_16 (and_16_out, not_4_out, not_3_out, not_2_out, e4);
  and and_17 (and_17_out, e1, e2, not_2_out);
  and and_18 (and_18_out, e1, not_3_out, e3, e4);
  or or_1 (d1, and_1_out, and_2_out);
  or or_2 (u3, and_7_out, and_8_out, and_9_out);
  or or_3 (d0, and_3_out, and_4_out, and_5_out, and_6_out);
  or or_4 (u2, and_10_out, and_11_out, and_12_out, and_13_out);
  or or_5 (u1, and_14_out, and_15_out, and_16_out, and_17_out, and_18_out);

  assign d2 = 1'b0;
  assign d3 = 1'b0;
  assign u0 = e0;
endmodule
