// Digital circuit intercambiador.dig as structural Verilog
module intercambiador (
  input  a3,
  input  a2,
  input  a1,
  input  a0,
  input  b3,
  input  b2,
  input  b1,
  input  b0,
  input  op,
  output ma,
  output eq,
  output me,
  output d0,
  output d1,
  output d2,
  output d3,
  output c0,
  output c1,
  output c2,
  output c3,
  output ne
);

  Comparator #(.Bits(4)) comparator_1 (.a({a3, a2, a1, a0}), .b({b3, b2, b1, b0}), .gt(ma), .eq(eq), .lt(me));
  and and_1 (ne, me, op);
  Multiplexer #(.Bits(4)) multiplexer_1 (
    .sel(ne), .in_0({a3, a2, a1, a0}), .in_1({b3, b2, b1, b0}), .out({c3, c2, c1, c0}));
  Multiplexer #(.Bits(4)) multiplexer_2 (
    .sel(ne), .in_0({b3, b2, b1, b0}), .in_1({a3, a2, a1, a0}), .out({d3, d2, d1, d0}));
endmodule
