// Digital circuit prueba7seg.dig as structural Verilog
module prueba7seg (
  input  c,
  input  g3,
  input  g2,
  input  g1,
  input  g0
);

  wire seg7_1_a, seg7_1_b, seg7_1_c, seg7_1_d, seg7_1_e, seg7_1_f, seg7_1_g;

  seg7 seg7_1 (
    .f3(g3), .f2(g2), .f1(g1), .f0(g0), .a(seg7_1_a), .b(seg7_1_b), .c(seg7_1_c), .d(seg7_1_d), .e(seg7_1_e),
    .f(seg7_1_f), .g(seg7_1_g));
  Seven_Seg #(.commonCathode("true"), .commonConnectionType("anode")) seven_seg_1 (
    .a(seg7_1_a), .b(seg7_1_b), .c(seg7_1_c), .d(seg7_1_d), .e(seg7_1_e), .f(seg7_1_f), .g(seg7_1_g), .dp(c),
    .common(c));
endmodule
