// Digital circuit seg7.dig as structural Verilog
module seg7 (
  input  f3,
  input  f2,
  input  f1,
  input  f0,
  output a,
  output b,
  output c,
  output d,
  output e,
  output f,
  output g
);

  wire and_1_out, and_2_out, and_3_out, and_4_out, and_6_out, and_7_out, and_8_out, and_9_out, and_10_out,
       and_11_out, and_12_out, and_13_out, and_14_out, and_15_out, and_16_out, and_17_out, and_18_out,
       not_1_out, not_2_out, not_3_out, not_4_out;

  not not_1 (not_1_out, f3);
  not not_2 (not_2_out, f2);
  not not_3 (not_3_out, f1);
  not not_4 (not_4_out, f0);
  and and_1 (and_1_out, f0, not_3_out, not_2_out, not_1_out);
  and and_2 (and_2_out, not_4_out, not_3_out, f2);
  and and_3 (and_3_out, f0, not_3_out, f2);
  and and_4 (and_4_out, not_4_out, f1, f2);
  and and_5 (c, not_4_out, f1, not_2_out);
  and and_6 (and_6_out, f0, not_3_out, not_2_out);
  and and_7 (and_7_out, not_4_out, not_3_out, f2);
  and and_8 (and_8_out, f0, f1, f2);
  and and_9 (and_9_out, f0, not_1_out);
  and and_10 (and_10_out, f0, not_3_out);
  and and_11 (and_11_out, f0, f2);
  and and_12 (and_12_out, not_3_out, f2);
  and and_13 (and_13_out, f0, not_2_out, not_1_out);
  and and_14 (and_14_out, f0, f1);
  and and_15 (and_15_out, f1, not_2_out);
  and and_16 (and_16_out, f0, f1, f2);
  and and_17 (and_17_out, f0, f1, f3);
  and and_18 (and_18_out, not_3_out, not_2_out, not_1_out);
  or or_1 (a, and_1_out, and_2_out);
  or or_2 (b, and_3_out, and_4_out);
  or or_3 (d, and_6_out, and_7_out, and_8_out);
  or or_4 (f, and_13_out, and_14_out, and_15_out);
  or or_5 (g, and_16_out, and_17_out, and_18_out);
  or or_6 (e, and_9_out, and_10_out, and_11_out, and_12_out);
endmodule
