// Digital circuit top.dig as structural Verilog
module top (
  input  a3,
  input  a2,
  input  a1,
  input  a0,
  input  b3,
  input  b2,
  input  b1,
  input  b0,
  input  op,
  input  r,
  input  enc,
  output ne,
  output a,
  output b,
  output c,
  output d,
  output e,
  output f,
  output g,
  output L1,
  output L2
);

  wire intercambiador_1_c0, intercambiador_1_c1, intercambiador_1_c2, intercambiador_1_c3,
       intercambiador_1_d0, intercambiador_1_d1, intercambiador_1_d2, intercambiador_1_d3, suma_resta_1_s0,
       suma_resta_1_s1, suma_resta_1_s2, suma_resta_1_s3, suma_resta_1_s4;
  wire [3:0] base_conversor_1_d3, base_conversor_1_u3, multiplexer_1_out;

  intercambiador intercambiador_1 (
    .a3(a3), .a2(a2), .a1(a1), .a0(a0), .b3(b3), .b2(b2), .b1(b1), .b0(b0), .op(op),
    .d0(intercambiador_1_d0), .d1(intercambiador_1_d1), .d2(intercambiador_1_d2), .d3(intercambiador_1_d3),
    .c0(intercambiador_1_c0), .c1(intercambiador_1_c1), .c2(intercambiador_1_c2), .c3(intercambiador_1_c3),
    .ne(ne));  // open: ma, eq, me
  Suma_resta suma_resta_1 (
    .a1(intercambiador_1_c1), .b1(intercambiador_1_d1), .a0(intercambiador_1_c0), .b0(intercambiador_1_d0),
    .a3(intercambiador_1_c3), .b3(intercambiador_1_d3), .a2(intercambiador_1_c2), .b2(intercambiador_1_d2),
    .Op(op), .s1(suma_resta_1_s1), .s0(suma_resta_1_s0), .s3(suma_resta_1_s3), .s2(suma_resta_1_s2),
    .s4(suma_resta_1_s4));
  base_conversor base_conversor_1 (
    .e4(suma_resta_1_s4), .e3(suma_resta_1_s3), .e2(suma_resta_1_s2), .e1(suma_resta_1_s1),
    .e0(suma_resta_1_s0), .d3(base_conversor_1_d3[3]), .d2(base_conversor_1_d3[2]),
    .d1(base_conversor_1_d3[1]), .d0(base_conversor_1_d3[0]), .u3(base_conversor_1_u3[3]),
    .u2(base_conversor_1_u3[2]), .u1(base_conversor_1_u3[1]), .u0(base_conversor_1_u3[0]));
  Multiplexer #(.Bits(4)) multiplexer_1 (
    .sel(r), .in_0(base_conversor_1_d3), .in_1(base_conversor_1_u3), .out(multiplexer_1_out));
  seg7 seg7_1 (
    .f3(multiplexer_1_out[3]), .f2(multiplexer_1_out[2]), .f1(multiplexer_1_out[1]),
    .f0(multiplexer_1_out[0]), .a(a), .b(b), .c(c), .d(d), .e(e), .f(f), .g(g));
  Demultiplexer demultiplexer_1 (.sel(r), .in(enc), .out_0(L1), .out_1(L2));

  // Notes on the sheet:
  //   r: Hz: 100
endmodule
