// Digital circuit Suma_resta.dig as structural Verilog
module Suma_resta (
  input  a1,
  input  b1,
  input  a0,
  input  b0,
  input  a3,
  input  b3,
  input  a2,
  input  b2,
  input  Op,
  output s1,
  output s0,
  output s3,
  output s2,
  output s4
);

  wire u_asig_2_cbo, u_asig_3_cbo, u_asig_4_cbo;

  asig #(.applicationType("IVERILOG"), .CodeFile("/home/desires/Documentos/Laboratorio 2/Sumador_restador/asig.v")) u_asig (
    .O(Op), .A(a3), .B(b3), .CBi(u_asig_2_cbo), .CBo(s4), .S(s3));
  asig #(.applicationType("IVERILOG"), .CodeFile("/home/desires/Documentos/Laboratorio 2/Sumador_restador/asig.v")) u_asig_2 (
    .O(Op), .A(a2), .B(b2), .CBi(u_asig_3_cbo), .CBo(u_asig_2_cbo), .S(s2));
  asig #(.applicationType("IVERILOG"), .CodeFile("/home/desires/Documentos/Laboratorio 2/Sumador_restador/asig.v")) u_asig_3 (
    .O(Op), .A(a1), .B(b1), .CBi(u_asig_4_cbo), .CBo(u_asig_3_cbo), .S(s1));
  asig #(.applicationType("IVERILOG"), .CodeFile("/home/desires/Documentos/Laboratorio 2/Sumador_restador/asig.v")) u_asig_4 (
    .O(Op), .A(a0), .B(b0), .CBi(1'b0), .CBo(u_asig_4_cbo), .S(s0));

  // Notes on the sheet:
  //   testbech
endmodule
