// Digital circuit fulladder.dig as structural Verilog
module fulladder (
  input  A,
  input  B,
  input  Ci,
  output Co,
  output S
);

  wire halfadder_1_co, halfadder_1_s, halfadder_2_co;

  halfadder halfadder_1 (.A(A), .B(B), .Co(halfadder_1_co), .S(halfadder_1_s));
  halfadder halfadder_2 (.A(Ci), .B(halfadder_1_s), .Co(halfadder_2_co), .S(S));
  or or_1 (Co, halfadder_1_co, halfadder_2_co);
endmodule
