// Digital circuit paralelladder.dig as structural Verilog
module paralelladder (
  input  a1,
  input  b1,
  input  a0,
  input  b0,
  input  a3,
  input  b3,
  input  a2,
  input  b2,
  output s1,
  output s0,
  output s3,
  output s2,
  output s4
);

  wire fulladder_2_co, fulladder_3_co, fulladder_4_co;

  fulladder fulladder_1 (.A(a3), .B(b3), .Ci(fulladder_2_co), .Co(s4), .S(s3));
  fulladder fulladder_2 (.A(a2), .B(b2), .Ci(fulladder_3_co), .Co(fulladder_2_co), .S(s2));
  fulladder fulladder_3 (.A(a1), .B(b1), .Ci(fulladder_4_co), .Co(fulladder_3_co), .S(s1));
  fulladder fulladder_4 (.A(a0), .B(b0), .Ci(1'b0), .Co(fulladder_4_co), .S(s0));
endmodule
