// Digital circuit 11bitsToBcd.dig as structural Verilog
module _11bitsToBcd (
  input  [10:0] l,
  output [3:0] m,
  output [3:0] c,
  output [3:0] d,
  output [3:0] u
);

  wire [2:0] bitstobcd_4_p2, bitstobcd_6_p2, bitstobcd_10_p2;
  wire [2:1] bitstobcd_4_p2_2;
  wire [3:0] bitstobcd_1_p2, bitstobcd_2_p2, bitstobcd_3_p2, bitstobcd_5_p2, bitstobcd_7_p2, bitstobcd_8_p2,
       bitstobcd_9_p2, bitstobcd_11_p2, bitstobcd_12_p2;

  // bitsToBcd bitstobcd_1: pin names not known; wires that end beside it: {1'b0, l[10:8]}, bitstobcd_1_p2
  // bitsToBcd bitstobcd_2: pin names not known; wires that end beside it: {bitstobcd_1_p2[2:0], l[7]}, bitstobcd_2_p2
  // bitsToBcd bitstobcd_3: pin names not known; wires that end beside it: {bitstobcd_2_p2[2:0], l[6]}, bitstobcd_3_p2
  // bitsToBcd bitstobcd_4: pin names not known; wires that end beside it: {1'b0, bitstobcd_1_p2[3], bitstobcd_2_p2[3], bitstobcd_3_p2[3]}, {bitstobcd_4_p2_2[2], bitstobcd_4_p2}
  // bitsToBcd bitstobcd_5: pin names not known; wires that end beside it: {bitstobcd_3_p2[2:0], l[5]}, bitstobcd_5_p2
  // bitsToBcd bitstobcd_6: pin names not known; wires that end beside it: {bitstobcd_4_p2, bitstobcd_5_p2[3]}, {bitstobcd_4_p2_2[1], bitstobcd_6_p2}
  // bitsToBcd bitstobcd_7: pin names not known; wires that end beside it: {bitstobcd_5_p2[2:0], l[4]}, bitstobcd_7_p2
  // bitsToBcd bitstobcd_8: pin names not known; wires that end beside it: {bitstobcd_6_p2, bitstobcd_7_p2[3]}, bitstobcd_8_p2
  // bitsToBcd bitstobcd_9: pin names not known; wires that end beside it: {bitstobcd_7_p2[2:0], l[3]}, bitstobcd_9_p2
  // bitsToBcd bitstobcd_10: pin names not known; wires that end beside it: {1'b0, bitstobcd_4_p2_2, bitstobcd_8_p2[3]}, {m[1], bitstobcd_10_p2}
  // bitsToBcd bitstobcd_11: pin names not known; wires that end beside it: {bitstobcd_8_p2[2:0], bitstobcd_9_p2[3]}, bitstobcd_11_p2
  // bitsToBcd bitstobcd_12: pin names not known; wires that end beside it: {bitstobcd_9_p2[2:0], l[2]}, bitstobcd_12_p2
  // bitsToBcd bitstobcd_13: pin names not known; wires that end beside it: {bitstobcd_10_p2, bitstobcd_11_p2[3]}, {m[0], c[3:1]}
  // bitsToBcd bitstobcd_14: pin names not known; wires that end beside it: {bitstobcd_11_p2[2:0], bitstobcd_12_p2[3]}, {c[0], d[3:1]}
  // bitsToBcd bitstobcd_15: pin names not known; wires that end beside it: {bitstobcd_12_p2[2:0], l[1]}, {d[0], u[3:1]}

  assign m[3:2] = 2'b00;
  assign u[0] = l[0];
endmodule
