// Digital circuit buzzer.dig as structural Verilog
module buzzer (
  input  cl,
  input  [8:0] d,
  output bu,
  output e_0
);

  wire and_1_out, comparator_1_lt, comparator_2_lt, d_ff_1_q, la_1_cl_o, multiplexer_1_out, not_1_out,
       not_2_out, si_1_cl_o;
  wire [25:0] counter_1_out, linea_1_c;

  not not_1 (not_1_out, d_ff_1_q);
  D_FF d_ff_1 (.D(comparator_1_lt), .C(cl), .Q(d_ff_1_q));  // open: nQ
  Counter #(.Bits(26)) counter_1 (.en(d_ff_1_q), .C(cl), .clr(not_1_out), .out(counter_1_out));  // open: ovf
  la la_1 (.cl_in(cl), .d(d), .cl_o(la_1_cl_o));
  si si_1 (.cl_in(cl), .cl_o(si_1_cl_o));
  linea linea_1 (.d(d), .e_0(e_0), .c(linea_1_c));
  Comparator #(.Bits(26)) comparator_1 (.a(counter_1_out), .b(linea_1_c), .lt(comparator_1_lt));  // open: gt, eq
  Multiplexer multiplexer_1 (.sel(e_0), .in_0(la_1_cl_o), .in_1(si_1_cl_o), .out(multiplexer_1_out));
  Multiplexer multiplexer_2 (.sel(and_1_out), .in_0(multiplexer_1_out), .in_1(1'b1), .out(bu));
  not not_2 (not_2_out, e_0);
  Comparator #(.Bits(26)) comparator_2 (.a(counter_1_out), .b(26'h4c4b40), .lt(comparator_2_lt));  // open: gt, eq
  and and_1 (and_1_out, not_2_out, comparator_2_lt);

  // Notes on the sheet:
  //   cl: Hz: 50000000
endmodule
