// Digital circuit cntr4.dig as structural Verilog
module cntr4 (
  input  cld,
  output [2:0] s
);

  wire not_1_out;

  not not_1 (not_1_out, 1'b1);
  Counter #(.Bits(3)) counter_1 (.en(1'b1), .C(cld), .clr(not_1_out), .out(s));  // open: ovf
endmodule
