// Digital circuit counting.dig as structural Verilog
module counting (
  input  t,
  input  c,
  input  cl,
  input  seg,
  output cu,
  output te,
  output ad
);

  wire and_1_out, and_2_out, and_3_out, and_4_out, and_5_out, comparator_1_gt, comparator_2_gt, d_ff_2_q,
       not_1_out, not_2_out, not_3_out, not_4_out, not_5_out, or_1_out, or_2_out, or_3_out, xor_1_out,
       xor_2_out;
  wire [4:0] counter_1_out, counter_2_out;

  not not_1 (not_1_out, t);
  and and_1 (and_1_out, cu, not_2_out, t);
  not not_2 (not_2_out, c);
  and and_2 (and_2_out, cu, not_3_out, t);
  not not_3 (not_3_out, c);
  and and_3 (and_3_out, not_1_out, c);
  and and_4 (and_4_out, cu, c);
  and and_5 (and_5_out, not_1_out, cu);
  or or_1 (or_1_out, and_3_out, and_4_out, and_5_out);
  or or_2 (or_2_out, and_1_out, comparator_1_gt);
  or or_3 (or_3_out, and_2_out, comparator_2_gt);
  xor xor_1 (xor_1_out, or_2_out, d_ff_2_q);
  xor xor_2 (xor_2_out, or_3_out, te);
  D_FF d_ff_1 (.D(or_1_out), .C(cl), .Q(cu));  // open: nQ
  and and_6 (ad, ~te, d_ff_2_q);  // And
  D_FF d_ff_2 (.D(xor_1_out), .C(cl), .Q(d_ff_2_q));  // open: nQ
  D_FF d_ff_3 (.D(xor_2_out), .C(cl), .Q(te));  // open: nQ
  not not_4 (not_4_out, d_ff_2_q);
  Counter #(.Bits(5)) counter_1 (.en(d_ff_2_q), .C(seg), .clr(not_4_out), .out(counter_1_out));  // open: ovf
  not not_5 (not_5_out, te);
  Counter #(.Bits(5)) counter_2 (.en(te), .C(seg), .clr(not_5_out), .out(counter_2_out));  // open: ovf
  Comparator #(.Bits(5)) comparator_1 (.a(counter_1_out), .b(5'b10011), .gt(comparator_1_gt));  // open: eq, lt
  Comparator #(.Bits(5)) comparator_2 (.a(counter_2_out), .b(5'b01001), .gt(comparator_2_gt));  // open: eq, lt
endmodule
