// Digital circuit cuarto_s.dig as structural Verilog
module cuarto_s (
  input  cl,
  output dvcl
);

  wire d_ff_1_nq, d_ff_1_q, d_ff_2_nq, d_ff_2_q, d_ff_3_nq, d_ff_3_q, d_ff_4_nq, d_ff_4_q, d_ff_5_nq,
       d_ff_5_q, d_ff_6_nq, d_ff_6_q, d_ff_7_nq, d_ff_7_q, d_ff_8_nq, d_ff_8_q, d_ff_9_nq, d_ff_9_q,
       d_ff_10_nq, d_ff_10_q, d_ff_11_nq, d_ff_11_q, d_ff_12_nq, d_ff_12_q, d_ff_13_nq, d_ff_13_q,
       d_ff_14_nq, d_ff_14_q, d_ff_15_nq, d_ff_15_q, d_ff_16_nq, d_ff_16_q, d_ff_17_nq, d_ff_17_q,
       d_ff_18_nq, d_ff_18_q, d_ff_19_nq, d_ff_19_q, d_ff_20_nq, d_ff_20_q, d_ff_21_nq, d_ff_21_q,
       d_ff_22_nq, d_ff_22_q, d_ff_23_nq, d_ff_23_q, d_ff_24_nq;

  D_FF d_ff_1 (.D(d_ff_1_nq), .C(cl), .Q(d_ff_1_q), .nQ(d_ff_1_nq));
  D_FF d_ff_2 (.D(d_ff_2_nq), .C(d_ff_21_q), .Q(d_ff_2_q), .nQ(d_ff_2_nq));
  D_FF d_ff_3 (.D(d_ff_3_nq), .C(d_ff_22_q), .Q(d_ff_3_q), .nQ(d_ff_3_nq));
  D_FF d_ff_4 (.D(d_ff_4_nq), .C(d_ff_23_q), .Q(d_ff_4_q), .nQ(d_ff_4_nq));
  D_FF d_ff_5 (.D(d_ff_5_nq), .C(d_ff_1_q), .Q(d_ff_5_q), .nQ(d_ff_5_nq));
  D_FF d_ff_6 (.D(d_ff_6_nq), .C(d_ff_2_q), .Q(d_ff_6_q), .nQ(d_ff_6_nq));
  D_FF d_ff_7 (.D(d_ff_7_nq), .C(d_ff_3_q), .Q(d_ff_7_q), .nQ(d_ff_7_nq));
  D_FF d_ff_8 (.D(d_ff_8_nq), .C(d_ff_4_q), .Q(d_ff_8_q), .nQ(d_ff_8_nq));
  D_FF d_ff_9 (.D(d_ff_9_nq), .C(d_ff_5_q), .Q(d_ff_9_q), .nQ(d_ff_9_nq));
  D_FF d_ff_10 (.D(d_ff_10_nq), .C(d_ff_6_q), .Q(d_ff_10_q), .nQ(d_ff_10_nq));
  D_FF d_ff_11 (.D(d_ff_11_nq), .C(d_ff_7_q), .Q(d_ff_11_q), .nQ(d_ff_11_nq));
  D_FF d_ff_12 (.D(d_ff_12_nq), .C(d_ff_8_q), .Q(d_ff_12_q), .nQ(d_ff_12_nq));
  D_FF d_ff_13 (.D(d_ff_13_nq), .C(d_ff_9_q), .Q(d_ff_13_q), .nQ(d_ff_13_nq));
  D_FF d_ff_14 (.D(d_ff_14_nq), .C(d_ff_10_q), .Q(d_ff_14_q), .nQ(d_ff_14_nq));
  D_FF d_ff_15 (.D(d_ff_15_nq), .C(d_ff_11_q), .Q(d_ff_15_q), .nQ(d_ff_15_nq));
  D_FF d_ff_16 (.D(d_ff_16_nq), .C(d_ff_12_q), .Q(d_ff_16_q), .nQ(d_ff_16_nq));
  D_FF d_ff_17 (.D(d_ff_17_nq), .C(d_ff_13_q), .Q(d_ff_17_q), .nQ(d_ff_17_nq));
  D_FF d_ff_18 (.D(d_ff_18_nq), .C(d_ff_14_q), .Q(d_ff_18_q), .nQ(d_ff_18_nq));
  D_FF d_ff_19 (.D(d_ff_19_nq), .C(d_ff_15_q), .Q(d_ff_19_q), .nQ(d_ff_19_nq));
  D_FF d_ff_20 (.D(d_ff_20_nq), .C(d_ff_16_q), .Q(d_ff_20_q), .nQ(d_ff_20_nq));
  D_FF d_ff_21 (.D(d_ff_21_nq), .C(d_ff_17_q), .Q(d_ff_21_q), .nQ(d_ff_21_nq));
  D_FF d_ff_22 (.D(d_ff_22_nq), .C(d_ff_18_q), .Q(d_ff_22_q), .nQ(d_ff_22_nq));
  D_FF d_ff_23 (.D(d_ff_23_nq), .C(d_ff_19_q), .Q(d_ff_23_q), .nQ(d_ff_23_nq));
  D_FF d_ff_24 (.D(d_ff_24_nq), .C(d_ff_20_q), .Q(dvcl), .nQ(d_ff_24_nq));
endmodule
