// Digital circuit cuenta.dig as structural Verilog
module cuenta (
  input  cl,
  output [8:0] c
);

  wire comparator_1_lt, comparator_2_lt, d_ff_1_q, d_ff_2_q, not_1_out, not_2_out;
  wire [8:0] counter_2_out;
  wire [25:0] counter_1_out;

  not not_1 (not_1_out, d_ff_1_q);
  D_FF d_ff_1 (.D(comparator_1_lt), .C(cl), .Q(d_ff_1_q));  // open: nQ
  Counter #(.Bits(26)) counter_1 (.en(d_ff_1_q), .C(cl), .clr(not_1_out), .out(counter_1_out));  // open: ovf
  not not_2 (not_2_out, d_ff_2_q);
  D_FF d_ff_2 (.D(comparator_2_lt), .C(cl), .Q(d_ff_2_q));  // open: nQ
  Counter #(.Bits(9)) counter_2 (
    .en(d_ff_2_q), .C(comparator_1_lt), .clr(not_2_out), .out(counter_2_out));  // open: ovf
  Comparator #(.Bits(26)) comparator_1 (.a(counter_1_out), .b(26'h2faf080), .lt(comparator_1_lt));  // open: gt, eq
  Comparator #(.Bits(9)) comparator_2 (.a(counter_2_out), .b(9'h14), .lt(comparator_2_lt));  // open: gt, eq
  Sub #(.Bits(9)) sub_1 (.a(9'h14), .b(counter_2_out), .c_i(1'b0), .s(c));  // open: c_o

  // Notes on the sheet:
  //   cl: Hz: 50000000
endmodule
