// Digital circuit distancia.dig as structural Verilog
module distancia (
  input  [19:0] cn,
  output [8:0] l,
  output [3:0] ld
);

  wire [39:0] mul_1_mul;

  Mul #(.Bits(20)) mul_1 (.a(20'h167), .b(cn), .mul({mul_1_mul[39:29], l, ld, mul_1_mul[15:0]}));
endmodule
