// Digital circuit frecuency.dig as structural Verilog
module frecuency (
  input  [8:0] d,
  output [19:0] f_2,
  output [19:0] f
);

  wire [39:0] mul_1_mul;
  wire [39:20] mul_2_mul;

  Mul #(.Bits(20)) mul_1 (.a({{11{1'b0}}, d}), .b(20'h1fb5), .mul(mul_1_mul));
  Add #(.Bits(20)) add_1 (.a(mul_1_mul[19:0]), .b(20'hfda7), .c_i(1'b0), .s(f_2));  // open: c_o
  Mul #(.Bits(20)) mul_2 (.a(f_2), .b(20'h2), .mul({mul_2_mul, f}));
endmodule
