// Digital circuit guarda.dig as structural Verilog
module guarda (
  input  gu,
  input  [3:0] gs_d,
  input  [3:0] gs_u,
  input  [3:0] gm_d,
  input  [3:0] gm_u,
  input  [3:0] gh_d,
  input  [3:0] gh_u,
  input  [3:0] gcm_m,
  input  [3:0] gcm_c,
  input  [3:0] gcm_d,
  input  [3:0] gcm_u,
  output [3:0] s_d,
  output [3:0] s_u,
  output [3:0] m_d,
  output [3:0] m_u,
  output [3:0] h_d,
  output [3:0] h_u,
  output [3:0] cm_m,
  output [3:0] cm_c,
  output [3:0] cm_d,
  output [3:0] cm_u
);

  D_FF #(.Bits(4)) d_ff_1 (.D(gs_d), .C(gu), .Q(s_d));  // open: nQ
  D_FF #(.Bits(4)) d_ff_2 (.D(gs_u), .C(gu), .Q(s_u));  // open: nQ
  D_FF #(.Bits(4)) d_ff_3 (.D(gm_d), .C(gu), .Q(m_d));  // open: nQ
  D_FF #(.Bits(4)) d_ff_4 (.D(gm_u), .C(gu), .Q(m_u));  // open: nQ
  D_FF #(.Bits(4)) d_ff_5 (.D(gh_d), .C(gu), .Q(h_d));  // open: nQ
  D_FF #(.Bits(4)) d_ff_6 (.D(gh_u), .C(gu), .Q(h_u));  // open: nQ
  D_FF #(.Bits(4)) d_ff_7 (.D(gcm_m), .C(gu), .Q(cm_m));  // open: nQ
  D_FF #(.Bits(4)) d_ff_8 (.D(gcm_c), .C(gu), .Q(cm_c));  // open: nQ
  D_FF #(.Bits(4)) d_ff_9 (.D(gcm_d), .C(gu), .Q(cm_d));  // open: nQ
  D_FF #(.Bits(4)) d_ff_10 (.D(gcm_u), .C(gu), .Q(cm_u));  // open: nQ
endmodule
