// Digital circuit la.dig as structural Verilog
module la (
  input  cl_in,
  input  [8:0] d,
  output cl_o
);

  wire comparator_1_lt, not_1_out;
  wire [19:0] counter_1_out, frecuency_1_f, frecuency_1_f_2;

  not not_1 (not_1_out, comparator_1_lt);
  Counter #(.Bits(20)) counter_1 (.en(comparator_1_lt), .C(cl_in), .clr(not_1_out), .out(counter_1_out));  // open: ovf
  frecuency frecuency_1 (.d(d), .f_2(frecuency_1_f_2), .f(frecuency_1_f));
  Comparator #(.Bits(20)) comparator_1 (.a(counter_1_out), .b(frecuency_1_f), .lt(comparator_1_lt));  // open: gt, eq
  Comparator #(.Bits(20)) comparator_2 (.a(counter_1_out), .b(frecuency_1_f_2), .lt(cl_o));  // open: gt, eq

  // Notes on the sheet:
  //   cl_in: Hz: 50000000
endmodule
