// Digital circuit led_h.dig as structural Verilog
module led_h (
  input  cen,
  input  uni,
  input  ll,
  output H
);

  wire and_1_out, and_2_out, not_1_out, not_2_out, not_3_out;

  not not_1 (not_1_out, cen);
  not not_2 (not_2_out, uni);
  not not_3 (not_3_out, ll);
  and and_1 (and_1_out, not_1_out, not_3_out);
  and and_2 (and_2_out, ll, not_2_out);
  or or_1 (H, and_1_out, and_2_out);
endmodule
