// Digital circuit linea.dig as structural Verilog
module linea (
  input  [8:0] d,
  output e_0,
  output [25:0] c
);

  wire comparator_1_lt;
  wire [19:0] multiplexer_1_out, sub_1_s;
  wire [39:0] mul_1_mul, mul_2_mul;

  Mul #(.Bits(20)) mul_1 (.a({{11{1'b0}}, d}), .b(20'h8edb6), .mul(mul_1_mul));
  Sub #(.Bits(20)) sub_1 (.a(mul_1_mul[32:13]), .b(20'h1ac), .c_i(1'b0), .s(sub_1_s));  // open: c_o
  Comparator #(.Bits(20)) comparator_1 (.a(mul_1_mul[32:13]), .b(20'h1ac), .lt(comparator_1_lt));  // open: gt, eq
  Multiplexer #(.Bits(20)) multiplexer_1 (
    .sel(comparator_1_lt), .in_0(sub_1_s), .in_1({20{1'b0}}), .out(multiplexer_1_out));
  Comparator #(.Bits(20)) comparator_2 (.a(multiplexer_1_out), .b({20{1'b0}}), .eq(e_0));  // open: gt, lt
  Mul #(.Bits(20)) mul_2 (.a(20'hc350), .b(multiplexer_1_out), .mul(mul_2_mul));
  Add #(.Bits(26)) add_1 (.a(mul_2_mul[25:0]), .b(26'h4c4b40), .c_i(1'b0), .s(c));  // open: c_o
endmodule
