// Digital circuit motor.dig as structural Verilog
module motor (
  input  cl,
  input  m,
  output smd,
  output vccm,
  output gndm,
  output l_01,
  output l_00
);

  wire comparator_1_lt, d_ff_1_q, demultiplexer_1_out_0, demultiplexer_1_out_1, not_1_out;
  wire [19:0] a0_1_p1, a90_1_p1, counter_1_out, ms20_1_p1, multiplexer_1_out;

  D_FF d_ff_1 (.D(comparator_1_lt), .C(cl), .Q(d_ff_1_q));  // open: nQ
  not not_1 (not_1_out, d_ff_1_q);
  Counter #(.Bits(20)) counter_1 (.en(d_ff_1_q), .C(cl), .clr(not_1_out), .out(counter_1_out));  // open: ovf
  // ms20 ms20_1: pin names not known; wires that end beside it: ms20_1_p1
  Comparator #(.Bits(20)) comparator_1 (.a(counter_1_out), .b(ms20_1_p1), .lt(comparator_1_lt));  // open: gt, eq
  // a0 a0_1: pin names not known; wires that end beside it: a0_1_p1
  // a90 a90_1: pin names not known; wires that end beside it: a90_1_p1
  Multiplexer #(.Bits(20)) multiplexer_1 (.sel(m), .in_0(a0_1_p1), .in_1(a90_1_p1), .out(multiplexer_1_out));
  Demultiplexer demultiplexer_1 (.sel(m), .in(1'b1), .out_0(demultiplexer_1_out_0), .out_1(demultiplexer_1_out_1));
  Comparator #(.Bits(20)) comparator_2 (.a(counter_1_out), .b(multiplexer_1_out), .lt(smd));  // open: gt, eq
  not not_2 (l_00, demultiplexer_1_out_0);
  not not_3 (l_01, demultiplexer_1_out_1);

  assign gndm = 1'b0;
  assign vccm = 1'b1;

  // Notes on the sheet:
  //   cl: Hz: 50000000
endmodule
