// Digital circuit precio (copia).dig as structural Verilog
module precio__copia (
  input  cl,
  input  cu,
  output [3:0] s_d,
  output [3:0] s_u,
  output [3:0] m_d,
  output [3:0] m_u,
  output [3:0] h_d,
  output [3:0] h_u,
  output [3:0] cm_m,
  output [3:0] cm_c,
  output [3:0] cm_d,
  output [3:0] cm_u
);

  wire and_1_out, and_2_out, and_3_out, and_4_out, comparator_1_lt, comparator_2_lt, comparator_3_lt,
       comparator_4_lt, multiplexer_1_out, multiplexer_2_out, multiplexer_3_out, multiplexer_4_out,
       not_1_out, not_2_out, not_3_out, not_4_out, not_5_out;
  wire [3:0] _9bitstobcd_1_p2, _9bitstobcd_1_p3, _9bitstobcd_2_p2, _9bitstobcd_2_p3, _9bitstobcd_3_p2,
       _9bitstobcd_3_p3, _11bitstobcd_1_c, _11bitstobcd_1_d, _11bitstobcd_1_m, _11bitstobcd_1_u;
  wire [8:0] _9bitstobcd_2_p1, _9bitstobcd_3_p1, counter_2_out;
  wire [10:0] counter_3_out;
  wire [26:0] counter_1_out;

  and and_1 (and_1_out, cu, comparator_1_lt);
  not not_1 (not_1_out, and_1_out);
  Counter #(.Bits(27)) counter_1 (.en(and_1_out), .C(cl), .clr(not_1_out), .out(counter_1_out));  // open: ovf
  and and_2 (and_2_out, cu, comparator_2_lt);
  Comparator #(.Bits(27)) comparator_1 (.a(counter_1_out), .b(27'h5f5e100), .lt(comparator_1_lt));  // open: gt, eq
  Multiplexer multiplexer_1 (.sel(cu), .in_0(cl), .in_1(comparator_1_lt), .out(multiplexer_1_out));
  not not_2 (not_2_out, and_2_out);
  Counter #(.Bits(9)) counter_2 (
    .en(and_2_out), .C(multiplexer_1_out), .clr(not_2_out), .out(counter_2_out));  // open: ovf
  // _9bitsToBcd _9bitstobcd_1: pin names not known; wires that end beside it: counter_2_out, _9bitstobcd_1_p2, _9bitstobcd_1_p3
  D_FF #(.Bits(4)) d_ff_1 (.D(_9bitstobcd_1_p2), .C(cl), .Q(s_d));  // open: nQ
  D_FF #(.Bits(4)) d_ff_2 (.D(_9bitstobcd_1_p3), .C(cl), .Q(s_u));  // open: nQ
  Comparator #(.Bits(9)) comparator_2 (.a(counter_2_out), .b(9'h3b), .lt(comparator_2_lt));  // open: gt, eq
  Multiplexer multiplexer_2 (.sel(cu), .in_0(cl), .in_1(not_2_out), .out(multiplexer_2_out));
  and and_3 (and_3_out, cu, comparator_3_lt);
  not not_3 (not_3_out, cu);
  Counter #(.Bits(11)) counter_3 (.en(cu), .C(multiplexer_2_out), .clr(not_3_out), .out(counter_3_out));  // open: ovf
  Multiplexer multiplexer_3 (.sel(cu), .in_0(cl), .in_1(comparator_2_lt), .out(multiplexer_3_out));
  // _9bitsToBcd _9bitstobcd_2: pin names not known; wires that end beside it: _9bitstobcd_2_p1, _9bitstobcd_2_p2, _9bitstobcd_2_p3
  not not_4 (not_4_out, and_3_out);
  Counter #(.Bits(9)) counter_4 (
    .en(and_3_out), .C(multiplexer_3_out), .clr(not_4_out), .out(_9bitstobcd_2_p1));  // open: ovf
  _11bitsToBcd _11bitstobcd_1 (
    .l(counter_3_out), .m(_11bitstobcd_1_m), .c(_11bitstobcd_1_c), .d(_11bitstobcd_1_d), .u(_11bitstobcd_1_u));
  D_FF #(.Bits(4)) d_ff_3 (.D(_9bitstobcd_2_p2), .C(cl), .Q(m_d));  // open: nQ
  D_FF #(.Bits(4)) d_ff_4 (.D(_9bitstobcd_2_p3), .C(cl), .Q(m_u));  // open: nQ
  Comparator #(.Bits(9)) comparator_3 (.a(_9bitstobcd_2_p1), .b(9'h3b), .lt(comparator_3_lt));  // open: gt, eq
  and and_4 (and_4_out, cu, comparator_4_lt);
  D_FF #(.Bits(4)) d_ff_5 (.D(_11bitstobcd_1_m), .C(cl), .Q(cm_m));  // open: nQ
  D_FF #(.Bits(4)) d_ff_6 (.D(_11bitstobcd_1_c), .C(cl), .Q(cm_c));  // open: nQ
  D_FF #(.Bits(4)) d_ff_7 (.D(_11bitstobcd_1_d), .C(cl), .Q(cm_d));  // open: nQ
  D_FF #(.Bits(4)) d_ff_8 (.D(_11bitstobcd_1_u), .C(cl), .Q(cm_u));  // open: nQ
  Multiplexer multiplexer_4 (.sel(cu), .in_0(cl), .in_1(comparator_3_lt), .out(multiplexer_4_out));
  // _9bitsToBcd _9bitstobcd_3: pin names not known; wires that end beside it: _9bitstobcd_3_p1, _9bitstobcd_3_p2, _9bitstobcd_3_p3
  not not_5 (not_5_out, and_4_out);
  Counter #(.Bits(9)) counter_5 (
    .en(and_4_out), .C(multiplexer_4_out), .clr(not_5_out), .out(_9bitstobcd_3_p1));  // open: ovf
  D_FF #(.Bits(4)) d_ff_9 (.D(_9bitstobcd_3_p2), .C(cl), .Q(h_d));  // open: nQ
  D_FF #(.Bits(4)) d_ff_10 (.D(_9bitstobcd_3_p3), .C(cl), .Q(h_u));  // open: nQ
  Comparator #(.Bits(9)) comparator_4 (.a(_9bitstobcd_3_p1), .b(9'h1e), .lt(comparator_4_lt));  // open: gt, eq

  // Notes on the sheet:
  //   cl: Hz: 50000000
endmodule
