// Digital circuit precio2.dig as structural Verilog
module precio2 (
  input  cl,
  input  cu,
  input  clr,
  output [3:0] s_d,
  output [3:0] s_u,
  output [3:0] m_d,
  output [3:0] m_u,
  output [3:0] h_d,
  output [3:0] h_u,
  output [3:0] cm_m,
  output [3:0] cm_c,
  output [3:0] cm_d,
  output [3:0] cm_u
);

  wire and_1_out, and_2_out, and_3_out, and_4_out, and_5_out, and_6_out, and_7_out, and_8_out, and_9_out,
       and_10_out, and_11_out, and_12_out, and_13_out, and_14_out, and_15_out, and_16_out, and_17_out,
       and_18_out, and_19_out, and_20_out, and_21_out, and_22_out, and_23_out, and_24_out, and_25_out,
       and_26_out, and_27_out, comparator_1_eq, comparator_1_lt, comparator_2_eq, comparator_2_lt,
       comparator_3_eq, comparator_3_lt, comparator_4_lt, comparator_5_lt, d_ff_1_q, d_ff_2_q, d_ff_5_q,
       multiplexer_1_out, multiplexer_2_out, multiplexer_3_out, multiplexer_4_out, not_1_out, not_2_out,
       or_1_out, or_2_out, or_3_out, or_4_out;
  wire [3:0] _9bitstobcd_1_p2, _9bitstobcd_1_p3, _9bitstobcd_2_p2, _9bitstobcd_2_p3, _9bitstobcd_3_p2,
       _9bitstobcd_3_p3, _11bitstobcd_1_c, _11bitstobcd_1_d, _11bitstobcd_1_m, _11bitstobcd_1_u;
  wire [8:0] counter_2_out, counter_4_out, counter_5_out;
  wire [10:0] add_1_s, counter_3_out;
  wire [26:0] counter_1_out;

  D_FF d_ff_1 (.D(cu), .C(cl), .Q(d_ff_1_q));  // open: nQ
  and and_1 (and_1_out, ~d_ff_1_q, cl, cu);  // And
  and and_2 (and_2_out, cl, ~and_1_out);  // And
  not not_1 (not_1_out, d_ff_1_q);
  and and_3 (and_3_out, comparator_1_lt, d_ff_1_q);
  Counter #(.Bits(27)) counter_1 (.en(and_3_out), .C(cl), .clr(not_2_out), .out(counter_1_out));  // open: ovf
  not not_2 (not_2_out, and_3_out);
  Comparator #(.Bits(27)) comparator_1 (
    .a(counter_1_out), .b(27'h2faf080), .eq(comparator_1_eq), .lt(comparator_1_lt));  // open: gt
  and and_4 (and_4_out, comparator_2_lt, ~not_1_out);  // And
  Multiplexer multiplexer_1 (.sel(not_1_out), .in_0(comparator_1_eq), .in_1(and_2_out), .out(multiplexer_1_out));
  Counter #(.Bits(9)) counter_2 (
    .en(and_4_out), .C(multiplexer_1_out), .clr(or_1_out), .out(counter_2_out));  // open: ovf
  or or_1 (or_1_out, and_9_out, and_7_out, and_5_out);
  and and_5 (and_5_out, clr, and_6_out);
  and and_6 (and_6_out, ~and_4_out, ~d_ff_1_q);  // And
  and and_7 (and_7_out, ~clr, and_8_out);  // And
  and and_8 (and_8_out, ~and_4_out, d_ff_1_q);  // And
  // _9bitsToBcd _9bitstobcd_1: pin names not known; wires that end beside it: counter_2_out, _9bitstobcd_1_p2, _9bitstobcd_1_p3
  Comparator #(.Bits(9)) comparator_2 (
    .a(counter_2_out), .b(9'h3b), .eq(comparator_2_eq), .lt(comparator_2_lt));  // open: gt
  and and_9 (and_9_out, clr, and_8_out);
  D_FF d_ff_2 (.D(comparator_2_eq), .C(multiplexer_1_out), .Q(d_ff_2_q));  // open: nQ
  D_FF #(.Bits(4)) d_ff_3 (.D(_9bitstobcd_1_p2), .C(multiplexer_1_out), .Q(s_d));  // open: nQ
  Multiplexer multiplexer_2 (.sel(not_1_out), .in_0(comparator_2_eq), .in_1(and_2_out), .out(multiplexer_2_out));
  D_FF #(.Bits(4)) d_ff_4 (.D(_9bitstobcd_1_p3), .C(multiplexer_1_out), .Q(s_u));  // open: nQ
  and and_10 (and_10_out, comparator_3_lt, ~not_1_out);  // And
  Multiplexer multiplexer_3 (.sel(not_1_out), .in_0(d_ff_2_q), .in_1(and_2_out), .out(multiplexer_3_out));
  and and_11 (and_11_out, comparator_4_lt, ~not_1_out);  // And
  or or_2 (or_2_out, and_20_out, and_18_out, and_12_out);
  Counter #(.Bits(11)) counter_3 (
    .en(and_11_out), .C(multiplexer_2_out), .clr(or_3_out), .out(counter_3_out));  // open: ovf
  or or_3 (or_3_out, and_21_out, and_16_out, and_13_out);
  Counter #(.Bits(9)) counter_4 (
    .en(and_10_out), .C(multiplexer_3_out), .clr(or_2_out), .out(counter_4_out));  // open: ovf
  and and_12 (and_12_out, clr, and_14_out);
  and and_13 (and_13_out, clr, and_15_out);
  and and_14 (and_14_out, ~and_10_out, ~d_ff_1_q);  // And
  and and_15 (and_15_out, ~and_11_out, ~d_ff_1_q);  // And
  and and_16 (and_16_out, ~clr, and_19_out);  // And
  and and_17 (and_17_out, ~and_10_out, d_ff_1_q);  // And
  and and_18 (and_18_out, ~clr, and_17_out);  // And
  and and_19 (and_19_out, ~and_11_out, d_ff_1_q);  // And
  // _9bitsToBcd _9bitstobcd_2: pin names not known; wires that end beside it: counter_4_out, _9bitstobcd_2_p2, _9bitstobcd_2_p3
  Comparator #(.Bits(9)) comparator_3 (
    .a(counter_4_out), .b(9'h3b), .eq(comparator_3_eq), .lt(comparator_3_lt));  // open: gt
  and and_20 (and_20_out, clr, and_17_out);
  D_FF d_ff_5 (.D(comparator_3_eq), .C(multiplexer_1_out), .Q(d_ff_5_q));  // open: nQ
  and and_21 (and_21_out, clr, and_19_out);
  Comparator #(.Bits(11)) comparator_4 (.a(counter_3_out), .b(11'h708), .lt(comparator_4_lt));  // open: gt, eq
  Add #(.Bits(11)) add_1 (.a(counter_3_out), .b(11'h1), .c_i(1'b0), .s(add_1_s));  // open: c_o
  D_FF #(.Bits(4)) d_ff_6 (.D(_9bitstobcd_2_p2), .C(multiplexer_1_out), .Q(m_d));  // open: nQ
  D_FF #(.Bits(4)) d_ff_7 (.D(_9bitstobcd_2_p3), .C(multiplexer_1_out), .Q(m_u));  // open: nQ
  and and_22 (and_22_out, comparator_5_lt, ~not_1_out);  // And
  Multiplexer multiplexer_4 (.sel(not_1_out), .in_0(d_ff_5_q), .in_1(and_2_out), .out(multiplexer_4_out));
  _11bitsToBcd _11bitstobcd_1 (
    .l(add_1_s), .m(_11bitstobcd_1_m), .c(_11bitstobcd_1_c), .d(_11bitstobcd_1_d), .u(_11bitstobcd_1_u));
  or or_4 (or_4_out, and_27_out, and_25_out, and_24_out);
  D_FF #(.Bits(4)) d_ff_8 (.D(_11bitstobcd_1_m), .C(multiplexer_1_out), .Q(cm_m));  // open: nQ
  Counter #(.Bits(9)) counter_5 (
    .en(and_22_out), .C(multiplexer_4_out), .clr(or_4_out), .out(counter_5_out));  // open: ovf
  D_FF #(.Bits(4)) d_ff_9 (.D(_11bitstobcd_1_c), .C(multiplexer_1_out), .Q(cm_c));  // open: nQ
  and and_23 (and_23_out, ~and_22_out, ~d_ff_1_q);  // And
  and and_24 (and_24_out, clr, and_23_out);
  D_FF #(.Bits(4)) d_ff_10 (.D(_11bitstobcd_1_d), .C(multiplexer_1_out), .Q(cm_d));  // open: nQ
  and and_25 (and_25_out, ~clr, and_26_out);  // And
  // _9bitsToBcd _9bitstobcd_3: pin names not known; wires that end beside it: counter_5_out, _9bitstobcd_3_p2, _9bitstobcd_3_p3
  and and_26 (and_26_out, ~and_22_out, d_ff_1_q);  // And
  and and_27 (and_27_out, clr, and_26_out);
  D_FF #(.Bits(4)) d_ff_11 (.D(_11bitstobcd_1_u), .C(multiplexer_1_out), .Q(cm_u));  // open: nQ
  Comparator #(.Bits(9)) comparator_5 (.a(counter_5_out), .b(9'h1d), .lt(comparator_5_lt));  // open: gt, eq
  D_FF #(.Bits(4)) d_ff_12 (.D(_9bitstobcd_3_p2), .C(multiplexer_1_out), .Q(h_d));  // open: nQ
  D_FF #(.Bits(4)) d_ff_13 (.D(_9bitstobcd_3_p3), .C(multiplexer_1_out), .Q(h_u));  // open: nQ

  // Notes on the sheet:
  //   cl: Hz: 150
endmodule
