// Digital circuit prueba127.dig as structural Verilog
module prueba127 (
  input  cl,
  output smd,
  output VCC,
  output GND,
  output l_01,
  output l_10,
  output l_11,
  output l_00
);

  wire comparator_1_lt, comparator_2_lt, d_ff_1_q, d_ff_2_q, demultiplexer_1_out_0, demultiplexer_1_out_1,
       demultiplexer_1_out_2, demultiplexer_1_out_3, not_1_out, not_2_out, not_3_out;
  wire [1:0] counter_3_out;
  wire [19:0] counter_1_out, ms2p54_1_p1, ms20_1_p1, multiplexer_1_out;
  wire [25:0] counter_2_out, s_1_s;

  D_FF d_ff_1 (.D(comparator_1_lt), .C(cl), .Q(d_ff_1_q));  // open: nQ
  not not_1 (not_1_out, d_ff_1_q);
  Counter #(.Bits(20)) counter_1 (.en(d_ff_1_q), .C(cl), .clr(not_1_out), .out(counter_1_out));  // open: ovf
  // ms20 ms20_1: pin names not known; wires that end beside it: ms20_1_p1
  D_FF d_ff_2 (.D(comparator_2_lt), .C(cl), .Q(d_ff_2_q));  // open: nQ
  not not_2 (not_2_out, 1'b1);
  not not_3 (not_3_out, d_ff_2_q);
  Counter #(.Bits(26)) counter_2 (.en(d_ff_2_q), .C(cl), .clr(not_3_out), .out(counter_2_out));  // open: ovf
  s s_1 (.s(s_1_s));
  Comparator #(.Bits(20)) comparator_1 (.a(counter_1_out), .b(ms20_1_p1), .lt(comparator_1_lt));  // open: gt, eq
  // ms2p54 ms2p54_1: pin names not known; wires that end beside it: ms2p54_1_p1
  Counter #(.Bits(2)) counter_3 (.en(1'b1), .C(comparator_2_lt), .clr(not_2_out), .out(counter_3_out));  // open: ovf
  Comparator #(.Bits(26)) comparator_2 (.a(counter_2_out), .b(s_1_s), .lt(comparator_2_lt));  // open: gt, eq
  Multiplexer #(.Selector_Bits(2), .Bits(20)) multiplexer_1 (
    .sel(counter_3_out), .in_0(ms2p54_1_p1), .in_1(ms2p54_1_p1), .in_2(ms2p54_1_p1), .in_3(ms2p54_1_p1),
    .out(multiplexer_1_out));
  Demultiplexer #(.Selector_Bits(2)) demultiplexer_1 (
    .sel(counter_3_out), .in(1'b1), .out_0(demultiplexer_1_out_0), .out_1(demultiplexer_1_out_1),
    .out_2(demultiplexer_1_out_2), .out_3(demultiplexer_1_out_3));
  Comparator #(.Bits(20)) comparator_3 (.a(counter_1_out), .b(multiplexer_1_out), .lt(smd));  // open: gt, eq
  not not_4 (l_00, demultiplexer_1_out_0);
  not not_5 (l_01, demultiplexer_1_out_1);
  not not_6 (l_10, demultiplexer_1_out_2);
  not not_7 (l_11, demultiplexer_1_out_3);

  assign GND = 1'b0;
  assign VCC = 1'b1;

  // Notes on the sheet:
  //   cl: Hz: 50000000
endmodule
