// Digital circuit seg.dig as structural Verilog
module seg (
  input  cl_in,
  output cl_o
);

  wire not_1_out;
  wire [25:0] counter_1_out;

  not not_1 (not_1_out, cl_o);
  Counter #(.Bits(26)) counter_1 (.en(cl_o), .C(cl_in), .clr(not_1_out), .out(counter_1_out));  // open: ovf
  Comparator #(.Bits(26)) comparator_1 (.a(counter_1_out), .b(26'h2faf080), .lt(cl_o));  // open: gt, eq
endmodule
