// Digital circuit seg3.dig as structural Verilog
module seg3 (
  input  cl_in,
  output cl_o
);

  wire not_1_out;
  wire [29:0] counter_1_out;

  not not_1 (not_1_out, cl_o);
  Counter #(.Bits(30)) counter_1 (.en(cl_o), .C(cl_in), .clr(not_1_out), .out(counter_1_out));  // open: ovf
  Comparator #(.Bits(30)) comparator_1 (.a(counter_1_out), .b(30'h2faf07f), .lt(cl_o));  // open: gt, eq
endmodule
