// Digital circuit sensor.dig as structural Verilog
module sensor (
  input  cl,
  input  ec,
  output Tri,
  output L_4,
  output L_3,
  output L_2,
  output L_1,
  output A,
  output B,
  output C,
  output D,
  output E,
  output F,
  output G,
  output H,
  output [8:0] d_2,
  output VCC,
  output GND,
  output L_8,
  output L_7,
  output L_6,
  output L_5,
  output bell,
  output lec
);

  wire cen, demultiplexer_1_out_1, demultiplexer_1_out_3, divfl_1_p2, eq_1_p2, eq_2_p2, hide_1_p3, hide_1_p4,
       ll, nollego_1_p2, not_1_out, uni;
  wire [1:0] cntr4_1_p2;
  wire [3:0] _9bitstobcd_1_p2, _9bitstobcd_1_p3, _9bitstobcd_1_p4, ctr_1_p1, d_ff_1_q, d_ff_2_q, d_ff_4_q,
       d_ff_5_q, distancia_1_ld, fraccion_1_p2, multiplexer_1_out_2, multiplexer_2_out, multiplexer_3_out,
       multiplexer_4_out;
  wire [15:0] f_alc_1_p1, multiplexer_1_out;
  wire [19:0] cntr_1_p3, relojc_1_p2;

  // relojC relojc_1: pin names not known; wires that end beside it: cl, relojc_1_p2
  // cntr cntr_1: pin names not known; wires that end beside it: ec, cl, cntr_1_p3
  // divFl divfl_1: pin names not known; wires that end beside it: cl, divfl_1_p2
  tpulso tpulso_1 (.l(relojc_1_p2), .ov(Tri));
  distancia distancia_1 (.cn(cntr_1_p3), .l(d_2), .ld(distancia_1_ld));
  // cntr4 cntr4_1: pin names not known; wires that end beside it: divfl_1_p2, cntr4_1_p2
  // Nollego nollego_1: pin names not known; wires that end beside it: d_2, nollego_1_p2
  // f_alc f_alc_1: pin names not known; wires that end beside it: f_alc_1_p1
  // _9bitsToBcd _9bitstobcd_1: pin names not known; wires that end beside it: d_2, _9bitstobcd_1_p2, _9bitstobcd_1_p3, _9bitstobcd_1_p4
  // fraccion fraccion_1: pin names not known; wires that end beside it: distancia_1_ld, fraccion_1_p2
  Multiplexer #(.Bits(16)) multiplexer_1 (
    .sel(nollego_1_p2), .in_0(f_alc_1_p1),
    .in_1({_9bitstobcd_1_p2, _9bitstobcd_1_p3, _9bitstobcd_1_p4, fraccion_1_p2}),
    .out({multiplexer_1_out[15:12], multiplexer_1_out_2, multiplexer_1_out[7:0]}));
  Demultiplexer #(.Selector_Bits(2)) demultiplexer_1 (
    .sel(cntr4_1_p2), .in(1'b1), .out_0(cen), .out_1(demultiplexer_1_out_1), .out_2(uni),
    .out_3(demultiplexer_1_out_3));
  not not_1 (not_1_out, ec);
  D_FF #(.Bits(4)) d_ff_1 (.D(multiplexer_1_out[15:12]), .C(not_1_out), .Q(d_ff_1_q));  // open: nQ
  D_FF #(.Bits(4)) d_ff_2 (.D(multiplexer_1_out_2), .C(not_1_out), .Q(d_ff_2_q));  // open: nQ
  not not_2 (L_4, cen);
  not not_3 (L_3, demultiplexer_1_out_1);
  not not_4 (L_2, uni);
  not not_5 (L_1, demultiplexer_1_out_3);
  // eq eq_1: pin names not known; wires that end beside it: d_ff_1_q, eq_1_p2
  // eq eq_2: pin names not known; wires that end beside it: d_ff_2_q, eq_2_p2
  // hide hide_1: pin names not known; wires that end beside it: eq_1_p2, eq_2_p2, hide_1_p3, hide_1_p4
  Multiplexer #(.Bits(4)) multiplexer_2 (.sel(hide_1_p3), .in_0(ctr_1_p1), .in_1(d_ff_1_q), .out(multiplexer_2_out));
  Multiplexer #(.Bits(4)) multiplexer_3 (.sel(hide_1_p4), .in_0(ctr_1_p1), .in_1(d_ff_2_q), .out(multiplexer_3_out));
  // ctr ctr_1: pin names not known; wires that end beside it: ctr_1_p1
  D_FF d_ff_3 (.D(nollego_1_p2), .C(not_1_out), .Q(ll));  // open: nQ
  D_FF #(.Bits(4)) d_ff_4 (.D(multiplexer_1_out[7:4]), .C(not_1_out), .Q(d_ff_4_q));  // open: nQ
  D_FF #(.Bits(4)) d_ff_5 (.D(multiplexer_1_out[3:0]), .C(not_1_out), .Q(d_ff_5_q));  // open: nQ
  Multiplexer #(.Selector_Bits(2), .Bits(4)) multiplexer_4 (
    .sel(cntr4_1_p2), .in_0(multiplexer_2_out), .in_1(multiplexer_3_out), .in_2(d_ff_4_q), .in_3(d_ff_5_q),
    .out(multiplexer_4_out));
  // seg7 seg7_1: pin names not known; wires that end beside it: multiplexer_4_out, {G, F, E, D, C, B, A}
  led_h led_h_1 (.cen(cen), .uni(uni), .ll(ll), .H(H));

  assign bell = 1'b0;
  assign GND = 1'b0;
  assign L_5 = 1'b1;
  assign L_6 = 1'b1;
  assign L_7 = 1'b1;
  assign L_8 = 1'b1;
  assign lec = ec;
  assign VCC = 1'b1;

  // Notes on the sheet:
  //   cl: Hz: 50000
endmodule
