// Digital circuit sensor2.dig as structural Verilog
module sensor2 (
  input  cl,
  input  ec,
  input  [3:0] m_d,
  input  [3:0] m_u,
  input  [3:0] s_d,
  input  [3:0] s_u,
  output Tri,
  output L_4,
  output L_3,
  output L_2,
  output L_1,
  output A,
  output B,
  output C,
  output D,
  output E,
  output F,
  output G,
  output H,
  output VCC,
  output GND,
  output L_8,
  output L_7,
  output L_6,
  output L_5,
  output bell,
  output lec,
  output bu,
  output ev,
  output e_0
);

  wire cen, comparator_1_eq, comparator_1_lt, demultiplexer_1_out_1, demultiplexer_1_out_3,
       demultiplexer_1_out_4, demultiplexer_1_out_5, demultiplexer_1_out_7, divfl_1_p2, eq_1_p2, eq_2_p2,
       hide_1_p3, hide_1_p4, led_h_1_h, ll, nollego_1_p2, not_1_out, p2, uni;
  wire [2:0] cntr4_1_s;
  wire [3:0] _9bitstobcd_1_p2, _9bitstobcd_1_p3, _9bitstobcd_1_p4, ctr_1_p1, d_ff_2_q, d_ff_3_q, d_ff_5_q,
       d_ff_6_q, distancia_1_ld, fraccion_1_p2, multiplexer_2_out_2, multiplexer_3_out, multiplexer_4_out,
       multiplexer_5_out;
  wire [8:0] d_ff_1_q, distancia_1_l, multiplexer_1_out;
  wire [15:0] f_alc_1_p1, multiplexer_2_out;
  wire [19:0] cntr_1_p3, relojc_1_p1;

  not not_1 (not_1_out, ec);
  // relojC relojc_1: pin names not known; wires that end beside it: relojc_1_p1, cl
  // cntr cntr_1: pin names not known; wires that end beside it: ec, cl, cntr_1_p3
  // divFl divfl_1: pin names not known; wires that end beside it: cl, divfl_1_p2
  tpulso tpulso_1 (.l(relojc_1_p1), .ov(Tri));
  D_FF #(.Bits(9)) d_ff_1 (.D(distancia_1_l), .C(not_1_out), .Q(d_ff_1_q));  // open: nQ
  distancia distancia_1 (.cn(cntr_1_p3), .l(distancia_1_l), .ld(distancia_1_ld));
  cntr4 cntr4_1 (.cld(divfl_1_p2), .s(cntr4_1_s));
  Multiplexer #(.Bits(9)) multiplexer_1 (.sel(ev), .in_0({9{1'b0}}), .in_1(d_ff_1_q), .out(multiplexer_1_out));
  Comparator #(.Bits(9)) comparator_1 (
    .a(d_ff_1_q), .b(9'h18), .eq(comparator_1_eq), .lt(comparator_1_lt));  // open: gt
  // Nollego nollego_1: pin names not known; wires that end beside it: distancia_1_l, nollego_1_p2
  // f_alc f_alc_1: pin names not known; wires that end beside it: f_alc_1_p1
  // _9bitsToBcd _9bitstobcd_1: pin names not known; wires that end beside it: distancia_1_l, _9bitstobcd_1_p2, _9bitstobcd_1_p3, _9bitstobcd_1_p4
  // fraccion fraccion_1: pin names not known; wires that end beside it: distancia_1_ld, fraccion_1_p2
  buzzer buzzer_1 (.cl(cl), .d(multiplexer_1_out), .bu(bu), .e_0(e_0));
  or or_1 (ev, comparator_1_lt, comparator_1_eq);
  Multiplexer #(.Bits(16)) multiplexer_2 (
    .sel(nollego_1_p2), .in_0(f_alc_1_p1),
    .in_1({_9bitstobcd_1_p2, _9bitstobcd_1_p3, _9bitstobcd_1_p4, fraccion_1_p2}),
    .out({multiplexer_2_out[15:12], multiplexer_2_out_2, multiplexer_2_out[7:0]}));
  Demultiplexer #(.Selector_Bits(3)) demultiplexer_1 (
    .sel(cntr4_1_s), .in(1'b1), .out_0(cen), .out_1(demultiplexer_1_out_1), .out_2(uni),
    .out_3(demultiplexer_1_out_3), .out_4(demultiplexer_1_out_4), .out_5(demultiplexer_1_out_5), .out_6(p2),
    .out_7(demultiplexer_1_out_7));
  D_FF #(.Bits(4)) d_ff_2 (.D(multiplexer_2_out[15:12]), .C(not_1_out), .Q(d_ff_2_q));  // open: nQ
  D_FF #(.Bits(4)) d_ff_3 (.D(multiplexer_2_out_2), .C(not_1_out), .Q(d_ff_3_q));  // open: nQ
  not not_2 (L_4, cen);
  not not_3 (L_3, demultiplexer_1_out_1);
  not not_4 (L_2, uni);
  not not_5 (L_1, demultiplexer_1_out_3);
  not not_6 (L_5, demultiplexer_1_out_4);
  not not_7 (L_6, demultiplexer_1_out_5);
  not not_8 (L_7, p2);
  not not_9 (L_8, demultiplexer_1_out_7);
  // eq eq_1: pin names not known; wires that end beside it: d_ff_2_q, eq_1_p2
  // eq eq_2: pin names not known; wires that end beside it: d_ff_3_q, eq_2_p2
  // hide hide_1: pin names not known; wires that end beside it: eq_1_p2, eq_2_p2, hide_1_p3, hide_1_p4
  Multiplexer #(.Bits(4)) multiplexer_3 (.sel(hide_1_p3), .in_0(ctr_1_p1), .in_1(d_ff_2_q), .out(multiplexer_3_out));
  Multiplexer #(.Bits(4)) multiplexer_4 (.sel(hide_1_p4), .in_0(ctr_1_p1), .in_1(d_ff_3_q), .out(multiplexer_4_out));
  // ctr ctr_1: pin names not known; wires that end beside it: ctr_1_p1
  D_FF d_ff_4 (.D(nollego_1_p2), .C(not_1_out), .Q(ll));  // open: nQ
  D_FF #(.Bits(4)) d_ff_5 (.D(multiplexer_2_out[7:4]), .C(not_1_out), .Q(d_ff_5_q));  // open: nQ
  D_FF #(.Bits(4)) d_ff_6 (.D(multiplexer_2_out[3:0]), .C(not_1_out), .Q(d_ff_6_q));  // open: nQ
  Multiplexer #(.Selector_Bits(3), .Bits(4)) multiplexer_5 (
    .sel(cntr4_1_s), .in_0(multiplexer_3_out), .in_1(multiplexer_4_out), .in_2(d_ff_5_q), .in_3(d_ff_6_q),
    .in_4(s_u), .in_5(s_d), .in_6(m_u), .in_7(m_d), .out(multiplexer_5_out));
  // seg7 seg7_1: pin names not known; wires that end beside it: multiplexer_5_out, {G, F, E, D, C, B, A}
  led_h led_h_1 (.cen(cen), .uni(uni), .ll(ll), .H(led_h_1_h));
  Multiplexer multiplexer_6 (.sel(p2), .in_0(led_h_1_h), .in_1(1'b0), .out(H));

  assign bell = 1'b0;
  assign GND = 1'b0;
  assign lec = ec;
  assign VCC = 1'b1;

  // Notes on the sheet:
  //   cl: Hz: 50000
endmodule
