// Digital circuit si.dig as structural Verilog
module si (
  input  cl_in,
  output cl_o
);

  wire comparator_1_lt, not_1_out;
  wire [16:0] counter_1_out;

  not not_1 (not_1_out, comparator_1_lt);
  Counter #(.Bits(17)) counter_1 (.en(comparator_1_lt), .C(cl_in), .clr(not_1_out), .out(counter_1_out));  // open: ovf
  Comparator #(.Bits(17)) comparator_1 (.a(counter_1_out), .b(17'hc5af), .lt(comparator_1_lt));  // open: gt, eq
  Comparator #(.Bits(17)) comparator_2 (.a(counter_1_out), .b(17'h62d8), .lt(cl_o));  // open: gt, eq
endmodule
