// Digital circuit top.dig as structural Verilog
module top (
  input  ec,
  input  cl,
  input  co,
  input  t,
  output led_v,
  output led_r,
  output bu,
  output smd,
  output vccm,
  output gndm,
  output Tri,
  output L_4,
  output L_3,
  output L_2,
  output L_1,
  output A,
  output B,
  output C,
  output D,
  output E,
  output F,
  output G,
  output H,
  output VCC,
  output GND,
  output L_8,
  output L_7,
  output L_6,
  output L_5,
  output bell,
  output lec,
  output seg,
  output ca,
  output cu,
  output e_1,
  output e_2,
  output e_3,
  output e_4
);

  wire and_2_out, and_3_out, and_4_out, and_5_out, and_6_out, and_8_out, and_9_out, counting_1_ad,
       counting_1_te, cuarto_s_1_dvcl, cun, d_ff_1_q, multiplexer_1_out, multiplexer_2_out, not_1_out,
       not_3_out, not_4_out, not_6_out, pal, prebu, sensor2_1_bu, sensor2_1_e_0, sensor2_1_ev;
  wire [3:0] guarda_1_m_d, guarda_1_m_u, guarda_1_s_d, guarda_1_s_u, m_d, m_u, precio2_1_cm_c,
       precio2_1_cm_d, precio2_1_cm_m, precio2_1_cm_u, precio2_1_h_d, precio2_1_h_u, precio2_1_m_d,
       precio2_1_m_u, precio2_1_s_d, precio2_1_s_u, s_d, s_u;

  sensor2 sensor2_1 (
    .cl(cl), .ec(ec), .m_d(m_d), .m_u(m_u), .s_d(s_d), .s_u(s_u), .Tri(Tri), .L_4(L_4), .L_3(L_3), .L_2(L_2),
    .L_1(L_1), .A(A), .B(B), .C(C), .D(D), .E(E), .F(F), .G(G), .H(H), .VCC(VCC), .GND(GND), .L_8(L_8),
    .L_7(L_7), .L_6(L_6), .L_5(L_5), .bell(bell), .lec(lec), .bu(sensor2_1_bu), .ev(sensor2_1_ev),
    .e_0(sensor2_1_e_0));
  seg seg_1 (.cl_in(cl), .cl_o(seg));
  not not_1 (not_1_out, cun);
  not not_2 (ca, and_5_out);
  and and_1 (prebu, not_1_out, cl);
  Multiplexer multiplexer_1 (.sel(sensor2_1_ev), .in_0(1'b0), .in_1(sensor2_1_bu), .out(multiplexer_1_out));
  and and_2 (and_2_out, t, and_5_out);
  and and_3 (and_3_out, co, and_5_out);
  and and_4 (and_4_out, cl, not_3_out);
  not not_3 (not_3_out, cun);
  cuarto_s cuarto_s_1 (.cl(cl), .dvcl(cuarto_s_1_dvcl));
  counting counting_1 (
    .t(and_2_out), .c(and_3_out), .cl(cl), .seg(seg), .cu(cun), .te(counting_1_te), .ad(counting_1_ad));
  and and_5 (and_5_out, sensor2_1_ev, sensor2_1_e_0);
  and and_6 (and_6_out, sensor2_1_ev, not_4_out);
  not not_4 (not_4_out, sensor2_1_e_0);
  D_FF d_ff_1 (.D(and_6_out), .C(and_4_out), .Q(d_ff_1_q));  // open: nQ
  not not_5 (led_v, sensor2_1_ev);
  motor motor_1 (.cl(cl), .m(d_ff_1_q), .smd(smd), .vccm(vccm), .gndm(gndm));  // open: l_01, l_00
  Multiplexer multiplexer_2 (.sel(pal), .in_0(1'b1), .in_1(cuarto_s_1_dvcl), .out(multiplexer_2_out));
  not not_6 (not_6_out, cun);
  and and_7 (led_r, multiplexer_2_out, sensor2_1_ev);
  and and_8 (and_8_out, not_6_out, multiplexer_1_out);
  and and_9 (and_9_out, ~counting_1_te, ~cun, ~counting_1_ad);  // And
  D_FF d_ff_2 (.D(and_8_out), .C(prebu), .Q(bu));  // open: nQ
  and and_10 (pal, not_6_out, and_5_out);
  not not_7 (cu, cun);
  not not_8 (e_1, and_9_out);
  not not_9 (e_2, cun);
  not not_10 (e_3, counting_1_te);
  not not_11 (e_4, counting_1_ad);
  precio2 precio2_1 (
    .cl(cl), .cu(cun), .clr(counting_1_ad), .s_d(precio2_1_s_d), .s_u(precio2_1_s_u), .m_d(precio2_1_m_d),
    .m_u(precio2_1_m_u), .h_d(precio2_1_h_d), .h_u(precio2_1_h_u), .cm_m(precio2_1_cm_m),
    .cm_c(precio2_1_cm_c), .cm_d(precio2_1_cm_d), .cm_u(precio2_1_cm_u));
  guarda guarda_1 (
    .gu(counting_1_te), .gs_d(precio2_1_s_d), .gs_u(precio2_1_s_u), .gm_d(precio2_1_m_d),
    .gm_u(precio2_1_m_u), .gh_d(precio2_1_h_d), .gh_u(precio2_1_h_u), .gcm_m(precio2_1_cm_m),
    .gcm_c(precio2_1_cm_c), .gcm_d(precio2_1_cm_d), .gcm_u(precio2_1_cm_u), .s_d(guarda_1_s_d),
    .s_u(guarda_1_s_u), .m_d(guarda_1_m_d), .m_u(guarda_1_m_u));  // open: h_d, h_u, cm_m, cm_c, cm_d, cm_u
  Multiplexer #(.Bits(4)) multiplexer_3 (.sel(counting_1_te), .in_0(precio2_1_s_d), .in_1(guarda_1_s_d), .out(s_d));
  Multiplexer #(.Bits(4)) multiplexer_4 (.sel(counting_1_te), .in_0(precio2_1_s_u), .in_1(guarda_1_s_u), .out(s_u));
  Multiplexer #(.Bits(4)) multiplexer_5 (.sel(counting_1_te), .in_0(precio2_1_m_d), .in_1(guarda_1_m_d), .out(m_d));
  Multiplexer #(.Bits(4)) multiplexer_6 (.sel(counting_1_te), .in_0(precio2_1_m_u), .in_1(guarda_1_m_u), .out(m_u));

  // Notes on the sheet:
  //   cl: Hz: 10
endmodule
